// Logisim project ex2.circ as structural Verilog: 1 circuit, main circuit compute_BrUn
module compute_BrUn (
  input  [31:0] INSTRUCTION,
  output BrUn
);

  Multiplexer #(.select(3)) multiplexer_1 (
    .in4(1'b0), .in5(1'b0), .in6(1'b1), .in7(1'b1), .out(BrUn), .sel(INSTRUCTION[14:12]));  // open: in0, in1, in2, in3
endmodule
