// Logisim project control-logic.circ as structural Verilog: 1 circuit, main circuit control_logic
module control_logic (
  input  [31:0] Instruction,
  input  BrEq,
  input  BrLt,
  output PCSel,
  output RegWEn,
  output [2:0] ImmSel,
  output BrUn,
  output ASel,
  output BSel,
  output [3:0] ALUSel,
  output MemWEn,
  output [1:0] WBSel
);

  wire and_30_out, and_31_out, and_32_out, and_33_out, and_34_out, and_35_out, and_45_out, and_46_out,
       B_type, I_type, is_add, is_addi, is_and, is_andi, is_auipc, is_beq, is_bge, is_bgeu, is_blt, is_bltu,
       is_bne, is_jal, is_jalr, is_lb, is_lh, is_lui, is_lw, is_mul, is_mulh, is_mulhu, is_or, is_ori, is_sb,
       is_sh, is_sll, is_slli, is_slt, is_slti, is_sra, is_srai, is_srl, is_srli, is_sub, is_sw, is_xor,
       is_xori, L_type, not_1_out, not_2_out, not_3_out, not_4_out, not_5_out, not_6_out, not_7_out,
       not_8_out, not_9_out, not_10_out, not_11_out, not_12_out, not_13_out, not_14_out, not_15_out,
       not_16_out, not_17_out, not_18_out, not_19_out, not_20_out, not_21_out, not_22_out, not_23_out,
       not_24_out, not_25_out, not_26_out, not_27_out, not_28_out, not_29_out, not_30_out, not_31_out,
       not_32_out, not_33_out, not_34_out, not_35_out, not_36_out, not_37_out, not_38_out, not_39_out,
       not_40_out, not_41_out, not_42_out, not_43_out, not_44_out, not_45_out, not_46_out, not_47_out,
       not_48_out, not_49_out, not_50_out, not_51_out, not_52_out, not_53_out, not_54_out, not_55_out,
       not_56_out, not_57_out, not_58_out, not_59_out, not_60_out, not_61_out, not_62_out, not_63_out,
       not_64_out, not_65_out, not_66_out, not_67_out, not_68_out, not_69_out, not_70_out, not_71_out,
       not_72_out, not_73_out, not_74_out, not_75_out, not_76_out, not_77_out, not_78_out, not_79_out,
       not_80_out, not_81_out, not_82_out, not_83_out, not_84_out, not_85_out, not_86_out, not_87_out,
       not_88_out, not_89_out, not_90_out, not_91_out, not_92_out, not_93_out, not_94_out, not_95_out,
       not_96_out, not_97_out, not_98_out, not_99_out, R_type, S_type;
  wire [5:0] address;
  wire [15:14] rom_1_data;

  not not_1 (not_1_out, Instruction[2]);
  not not_2 (not_2_out, Instruction[3]);
  and and_1 (I_type, not_1_out, not_2_out, Instruction[4], not_3_out, not_4_out);
  not not_3 (not_3_out, Instruction[5]);
  not not_4 (not_4_out, Instruction[6]);
  not not_5 (not_5_out, Instruction[12]);
  not not_6 (not_6_out, Instruction[13]);
  not not_7 (not_7_out, Instruction[14]);
  not not_8 (not_8_out, Instruction[12]);
  not not_9 (not_9_out, Instruction[12]);
  not not_10 (not_10_out, Instruction[13]);
  not not_11 (not_11_out, Instruction[30]);
  not not_12 (not_12_out, Instruction[13]);
  not not_13 (not_13_out, Instruction[14]);
  not not_14 (not_14_out, Instruction[30]);
  not not_15 (not_15_out, Instruction[13]);
  not not_16 (not_16_out, Instruction[13]);
  not not_17 (not_17_out, Instruction[12]);
  not not_18 (not_18_out, Instruction[14]);
  and and_2 (is_addi, not_5_out, not_6_out, not_7_out, I_type);
  and and_3 (is_andi, Instruction[12], Instruction[13], Instruction[14], I_type);
  and and_4 (is_ori, not_8_out, Instruction[13], Instruction[14], I_type);
  and and_5 (is_xori, not_9_out, not_10_out, Instruction[14], I_type);
  and and_6 (is_slli, Instruction[12], not_12_out, not_11_out, not_13_out, I_type);
  and and_7 (is_srli, Instruction[12], not_15_out, not_14_out, Instruction[14], I_type);
  and and_8 (is_srai, Instruction[12], not_16_out, Instruction[30], Instruction[14], I_type);
  and and_9 (is_slti, not_17_out, Instruction[13], not_18_out, I_type);
  ROM #(.addrWidth(6), .dataWidth(16)) rom_1 (
    .addr(address), .data({rom_1_data, WBSel, MemWEn, ALUSel, BSel, ASel, BrUn, ImmSel, RegWEn}));
  not not_19 (not_19_out, Instruction[2]);
  not not_20 (not_20_out, Instruction[3]);
  not not_21 (not_21_out, Instruction[6]);
  not not_22 (not_22_out, Instruction[30]);
  not not_23 (not_23_out, Instruction[12]);
  not not_24 (not_24_out, Instruction[13]);
  not not_25 (not_25_out, Instruction[14]);
  not not_26 (not_26_out, Instruction[12]);
  not not_27 (not_27_out, Instruction[13]);
  not not_28 (not_28_out, Instruction[14]);
  not not_29 (not_29_out, Instruction[30]);
  not not_30 (not_30_out, Instruction[30]);
  not not_31 (not_31_out, Instruction[12]);
  not not_32 (not_32_out, Instruction[30]);
  not not_33 (not_33_out, Instruction[12]);
  not not_34 (not_34_out, Instruction[13]);
  not not_35 (not_35_out, Instruction[25]);
  not not_36 (not_36_out, Instruction[13]);
  not not_37 (not_37_out, Instruction[14]);
  not not_38 (not_38_out, Instruction[30]);
  not not_39 (not_39_out, Instruction[13]);
  not not_40 (not_40_out, Instruction[13]);
  not not_41 (not_41_out, Instruction[30]);
  not not_42 (not_42_out, Instruction[12]);
  not not_43 (not_43_out, Instruction[14]);
  not not_44 (not_44_out, Instruction[12]);
  not not_45 (not_45_out, Instruction[13]);
  not not_46 (not_46_out, Instruction[14]);
  not not_47 (not_47_out, Instruction[13]);
  not not_48 (not_48_out, Instruction[14]);
  not not_49 (not_49_out, Instruction[14]);
  and and_10 (R_type, not_19_out, not_20_out, Instruction[4], Instruction[5], not_21_out);
  not not_50 (not_50_out, Instruction[25]);
  and and_11 (is_add, not_50_out, not_22_out, not_23_out, not_25_out, R_type, not_24_out);
  and and_12 (is_sub, Instruction[30], not_26_out, not_27_out, not_28_out, R_type);
  and and_13 (is_and, not_29_out, Instruction[12], Instruction[13], Instruction[14], R_type);
  and and_14 (is_or, not_30_out, not_31_out, Instruction[13], Instruction[14], R_type);
  and and_15 (is_xor, not_32_out, not_33_out, not_34_out, Instruction[14], R_type);
  and and_16 (is_sll, not_35_out, Instruction[12], not_36_out, not_37_out, R_type);
  and and_17 (is_srl, not_38_out, Instruction[12], not_39_out, Instruction[14], R_type);
  and and_18 (is_sra, Instruction[30], Instruction[12], not_40_out, Instruction[14], R_type);
  and and_19 (is_slt, not_41_out, not_42_out, Instruction[13], not_43_out, R_type);
  and and_20 (is_mul, Instruction[25], not_44_out, not_45_out, not_46_out, R_type);
  and and_21 (is_mulh, Instruction[25], Instruction[12], not_47_out, not_48_out, R_type);
  and and_22 (is_mulhu, Instruction[25], Instruction[12], Instruction[13], not_49_out, R_type);
  not not_51 (not_51_out, Instruction[2]);
  not not_52 (not_52_out, Instruction[3]);
  not not_53 (not_53_out, Instruction[4]);
  not not_54 (not_54_out, Instruction[12]);
  not not_55 (not_55_out, Instruction[13]);
  not not_56 (not_56_out, Instruction[14]);
  not not_57 (not_57_out, Instruction[13]);
  not not_58 (not_58_out, Instruction[12]);
  not not_59 (not_59_out, Instruction[13]);
  not not_60 (not_60_out, Instruction[12]);
  not not_61 (not_61_out, Instruction[13]);
  not not_62 (not_62_out, Instruction[14]);
  and and_23 (B_type, not_51_out, not_52_out, not_53_out, Instruction[5], Instruction[6]);
  and and_24 (is_beq, not_54_out, not_55_out, not_56_out, B_type);
  and and_25 (is_bge, Instruction[12], not_57_out, Instruction[14], B_type);
  and and_26 (is_bgeu, Instruction[12], Instruction[13], Instruction[14], B_type);
  and and_27 (is_blt, not_58_out, not_59_out, Instruction[14], B_type);
  and and_28 (is_bltu, not_60_out, Instruction[13], Instruction[14], B_type);
  and and_29 (is_bne, Instruction[12], not_61_out, not_62_out, B_type);
  not not_63 (not_63_out, BrEq);
  not not_64 (not_64_out, BrLt);
  not not_65 (not_65_out, BrLt);
  and and_30 (and_30_out, is_beq, BrEq);
  and and_31 (and_31_out, is_bne, not_63_out);
  and and_32 (and_32_out, is_blt, BrLt);
  and and_33 (and_33_out, is_bltu, BrLt);
  and and_34 (and_34_out, is_bge, not_64_out);
  and and_35 (and_35_out, is_bgeu, not_65_out);
  or or_1 (PCSel, is_jal, and_30_out, and_31_out, and_32_out, and_33_out, and_34_out, and_35_out, is_jalr);
  not not_66 (not_66_out, Instruction[2]);
  not not_67 (not_67_out, Instruction[3]);
  not not_68 (not_68_out, Instruction[4]);
  not not_69 (not_69_out, Instruction[5]);
  not not_70 (not_70_out, Instruction[6]);
  not not_71 (not_71_out, Instruction[12]);
  not not_72 (not_72_out, Instruction[13]);
  not not_73 (not_73_out, Instruction[14]);
  not not_74 (not_74_out, Instruction[13]);
  not not_75 (not_75_out, Instruction[14]);
  not not_76 (not_76_out, Instruction[12]);
  not not_77 (not_77_out, Instruction[14]);
  Priority_Encoder #(.select_enc(6)) priority_encoder_1 (
    .in0(is_addi), .in1(is_andi), .in2(is_ori), .in3(is_xori), .in4(is_slli), .in5(is_srli), .in6(is_srai),
    .in7(is_slti), .in8(is_add), .in9(is_sub), .in10(is_and), .in11(is_or), .in12(is_xor), .in13(is_sll),
    .in14(is_srl), .in15(is_sra), .in16(is_slt), .in17(is_mul), .in18(is_mulh), .in19(is_mulhu),
    .in20(is_beq), .in21(is_bge), .in22(is_bgeu), .in23(is_blt), .in24(is_bltu), .in25(is_bne), .in26(is_lb),
    .in27(is_lh), .in28(is_lw), .in29(is_sb), .in30(is_sh), .in31(is_sw), .in32(is_jal), .in33(is_jalr),
    .in34(is_auipc), .in35(is_lui), .out(address));  // open: in36, in37, in38, in39, in40, in41, in42, in43, in44, in45, in46, in47, in48, in49, in50, in51, in52, in53, in54, in55, in56, in57, in58, in59, in60, in61, in62, in63, gs, en_out, en_in
  and and_36 (L_type, not_66_out, not_67_out, not_68_out, not_69_out, not_70_out);
  and and_37 (is_lb, not_71_out, not_72_out, not_73_out, L_type);
  and and_38 (is_lh, Instruction[12], not_74_out, not_75_out, L_type);
  and and_39 (is_lw, not_76_out, Instruction[13], not_77_out, L_type);
  not not_78 (not_78_out, Instruction[2]);
  not not_79 (not_79_out, Instruction[3]);
  not not_80 (not_80_out, Instruction[4]);
  not not_81 (not_81_out, Instruction[6]);
  not not_82 (not_82_out, Instruction[12]);
  not not_83 (not_83_out, Instruction[13]);
  not not_84 (not_84_out, Instruction[14]);
  not not_85 (not_85_out, Instruction[13]);
  not not_86 (not_86_out, Instruction[14]);
  not not_87 (not_87_out, Instruction[12]);
  not not_88 (not_88_out, Instruction[14]);
  and and_40 (S_type, not_78_out, not_79_out, not_80_out, Instruction[5], not_81_out);
  and and_41 (is_sb, not_82_out, not_83_out, not_84_out, S_type);
  and and_42 (is_sh, Instruction[12], not_85_out, not_86_out, S_type);
  and and_43 (is_sw, not_87_out, Instruction[13], not_88_out, S_type);
  not not_89 (not_89_out, Instruction[4]);
  not not_90 (not_90_out, Instruction[3]);
  not not_91 (not_91_out, Instruction[4]);
  not not_92 (not_92_out, Instruction[12]);
  not not_93 (not_93_out, Instruction[13]);
  not not_94 (not_94_out, Instruction[14]);
  not not_95 (not_95_out, Instruction[3]);
  not not_96 (not_96_out, Instruction[5]);
  not not_97 (not_97_out, Instruction[6]);
  not not_98 (not_98_out, Instruction[3]);
  not not_99 (not_99_out, Instruction[6]);
  and and_44 (is_jal, Instruction[2], Instruction[3], not_89_out, Instruction[5], Instruction[6]);
  and and_45 (and_45_out, Instruction[2], not_90_out, not_91_out, Instruction[5], Instruction[6]);
  and and_46 (and_46_out, not_92_out, not_93_out, not_94_out);
  and and_47 (is_auipc, Instruction[2], not_95_out, Instruction[4], not_96_out, not_97_out);
  and and_48 (is_lui, Instruction[2], not_98_out, Instruction[4], Instruction[5], not_99_out);
  and and_49 (is_jalr, and_45_out, and_46_out);

  // Other names for the same wires on the sheet: i2 = Instruction[2]; i3 = Instruction[3]; i4 = Instruction[4];
  //   i5 = Instruction[5]; i6 = Instruction[6]; i12 = Instruction[12]; i13 = Instruction[13]; i14 = Instruction[14];
  //   i25 = Instruction[25]; i30 = Instruction[30]

  // Notes on the sheet:
  //   INPUTS to your circuit
  //   Connect ROM Input here ->
  //   I_type here doesn't contain lb/lh/lw, although they both are I-type, they have different opcode 
  //   contents of rom_1 (hex, n*v repeats v):
  //   1051 13d1 1351 1251 10d1 12d1 16d1 1151 1001 1601 1381 1301 1201 1081 1281 1681 1101 1401 1481 1581
  //   64 64 74 64 74 64 41 41 41 842 842 842 2069 2041 1067 17c7
  //   ROM FOR CONTROL LOGIC
  //   DON'T CHANGE THE LOCATIONS OF THE INPUTS AND OUTPUTS!
  //   This is only if you choose to do the ROM option
  //   OUTPUT from your circuit
endmodule
