// Logisim project imm-gen.circ as structural Verilog: 1 circuit, main circuit imm_gen
module imm_gen (
  input  [31:0] Instruction,
  input  [2:0] ImmSel,
  output [31:0] Immediate
);

  wire [31:11] I, S;
  wire [31:12] B;
  wire [31:20] J;

  Multiplexer #(.width(21)) multiplexer_1 (.in0({21{1'b0}}), .in1({21{1'b1}}), .out(I), .sel(Instruction[31]));
  Multiplexer #(.width(20)) multiplexer_2 (.in0({20{1'b0}}), .in1({20{1'b1}}), .out(B), .sel(Instruction[31]));
  Multiplexer #(.select(3), .width(32)) multiplexer_3 (
    .in0({I, Instruction[30:20]}), .in1({S, Instruction[30:25], Instruction[11:7]}),
    .in2({B, Instruction[7], Instruction[30:25], Instruction[11:8], 1'b0}),
    .in3({Instruction[31:12], {12{1'b0}}}),
    .in4({J, Instruction[19:12], Instruction[20], Instruction[30:21], 1'b0}), .out(Immediate), .sel(ImmSel));  // open: in5, in6, in7
  Multiplexer #(.width(21)) multiplexer_4 (.in0({21{1'b0}}), .in1({21{1'b1}}), .out(S), .sel(Instruction[31]));
  Multiplexer #(.width(12)) multiplexer_5 (.in0({12{1'b0}}), .in1({12{1'b1}}), .out(J), .sel(Instruction[31]));

  // Other names for the same wires on the sheet: I[10:0] = Instruction[30:20];
  //   J[19:1] = {Instruction[19:12], Instruction[20], Instruction[30:21]}; U[31:12] = Instruction[31:12];
  //   B[11:1] = {Instruction[7], Instruction[30:25], Instruction[11:8]};
  //   S[10:0] = {Instruction[30:25], Instruction[11:7]}

  // Notes on the sheet:
  //   INPUTS to your circuit
  //   I-type
  //   B-type
  //   DON'T CHANGE THE LOCATIONS OF THE INPUTS AND OUTPUTS!
  //   OUTPUT from your circuit
endmodule
