// Logisim project partial-load.circ as structural Verilog: 1 circuit, main circuit partial_load
module partial_load (
  input  [31:0] Instruction,
  input  [31:0] MemAddress,
  input  [31:0] DataFromMem,
  output [31:0] DataToReg
);

  wire L_type, lb, lh, lw, not_1_out, not_2_out, not_3_out, not_4_out, not_5_out, not_6_out, not_7_out,
       not_8_out, not_9_out, not_10_out, not_11_out, not_12_out, not_13_out, not_14_out, not_15_out,
       not_16_out, not_17_out;
  wire [1:0] priority_encoder_1_out;
  wire [7:7] multiplexer_1_out;
  wire [15:15] multiplexer_2_out;
  wire [31:0] lb_data, lh_data;

  not not_1 (not_1_out, Instruction[2]);
  not not_2 (not_2_out, Instruction[3]);
  not not_3 (not_3_out, Instruction[4]);
  not not_4 (not_4_out, Instruction[5]);
  not not_5 (not_5_out, Instruction[6]);
  not not_6 (not_6_out, Instruction[12]);
  not not_7 (not_7_out, Instruction[13]);
  not not_8 (not_8_out, Instruction[14]);
  not not_9 (not_9_out, Instruction[13]);
  not not_10 (not_10_out, Instruction[14]);
  not not_11 (not_11_out, Instruction[12]);
  not not_12 (not_12_out, Instruction[14]);
  and and_1 (L_type, not_1_out, not_2_out, not_3_out, not_4_out, not_5_out);
  and and_2 (lb, L_type, not_6_out, not_7_out, not_8_out);
  and and_3 (lh, L_type, Instruction[12], not_9_out, not_10_out);
  and and_4 (lw, L_type, not_11_out, Instruction[13], not_12_out);
  Multiplexer #(.select(2), .width(8)) multiplexer_1 (
    .in0(DataFromMem[7:0]), .in1(DataFromMem[15:8]), .in2(DataFromMem[23:16]), .in3(DataFromMem[31:24]),
    .out({multiplexer_1_out[7], lb_data[6:0]}), .sel(MemAddress[1:0]));
  Multiplexer #(.select(2), .width(16)) multiplexer_2 (
    .in0(DataFromMem[15:0]), .in1(DataFromMem[23:8]), .in2(DataFromMem[31:16]),
    .out({multiplexer_2_out[15], lh_data[14:0]}), .sel(MemAddress[1:0]));  // open: in3
  Priority_Encoder #(.select_enc(2)) priority_encoder_1 (
    .in0(lb), .in1(lh), .in2(lw), .out(priority_encoder_1_out));  // open: in3, gs, en_out, en_in
  Multiplexer #(.width(25)) multiplexer_3 (
    .in0({25{1'b0}}), .in1({25{1'b1}}), .out(lb_data[31:7]), .sel(multiplexer_1_out[7]));
  Multiplexer #(.width(17)) multiplexer_4 (
    .in0({17{1'b0}}), .in1({17{1'b1}}), .out(lh_data[31:15]), .sel(multiplexer_2_out[15]));
  Multiplexer #(.select(2), .width(32)) multiplexer_5 (
    .in0(lb_data), .in1(lh_data), .in2(DataFromMem), .out(DataToReg), .sel(priority_encoder_1_out));  // open: in3
  not not_13 (not_13_out, Instruction[2]);
  not not_14 (not_14_out, Instruction[3]);
  not not_15 (not_15_out, Instruction[4]);
  not not_16 (not_16_out, Instruction[5]);
  not not_17 (not_17_out, Instruction[6]);
  and and_5 (L_type, not_13_out, not_14_out, not_15_out, not_16_out, not_17_out);

  // Other names for the same wires on the sheet: D7_0[7:0] = DataFromMem[7:0]; D15_0[15:0] = DataFromMem[15:0];
  //   D15_8[7:0] = DataFromMem[15:8]; D23_8[15:0] = DataFromMem[23:8]; D23_16[7:0] = DataFromMem[23:16];
  //   D31_16[15:0] = DataFromMem[31:16]; D31_24[7:0] = DataFromMem[31:24]; i2 = Instruction[2]; i3 = Instruction[3];
  //   i4 = Instruction[4]; i5 = Instruction[5]; i6 = Instruction[6]; i12 = Instruction[12]; i13 = Instruction[13];
  //   i14 = Instruction[14]; A1_0[1:0] = MemAddress[1:0]

  // Notes on the sheet:
  //   INPUTS to your circuit
  //   DON'T CHANGE THE LOCATIONS OF THE INPUTS AND OUTPUTS!
  //   lb
  //   OUTPUT from your circuit
endmodule
