// Logisim project partial-store.circ as structural Verilog: 1 circuit, main circuit partial_store
module partial_store (
  input  [31:0] Instruction,
  input  [31:0] MemAddress,
  input  [31:0] DataFromReg,
  input  MemWEn,
  output [3:0] MemWriteMask,
  output [31:0] DataToMem
);

  wire not_1_out, not_2_out, not_3_out, not_4_out, not_5_out, not_6_out, not_7_out, not_8_out, not_9_out,
       not_10_out, not_11_out, R_type, sb, sh, sw;
  wire [1:0] which_type;
  wire [3:0] multiplexer_6_out, sb_mask, sh_mask;
  wire [31:0] sb_data, sh_data;

  not not_1 (not_1_out, Instruction[2]);
  not not_2 (not_2_out, Instruction[3]);
  not not_3 (not_3_out, Instruction[4]);
  not not_4 (not_4_out, Instruction[6]);
  not not_5 (not_5_out, Instruction[12]);
  not not_6 (not_6_out, Instruction[13]);
  not not_7 (not_7_out, Instruction[14]);
  not not_8 (not_8_out, Instruction[13]);
  not not_9 (not_9_out, Instruction[14]);
  not not_10 (not_10_out, Instruction[12]);
  not not_11 (not_11_out, Instruction[14]);
  and and_1 (R_type, not_1_out, not_2_out, not_3_out, Instruction[5], not_4_out);
  and and_2 (sb, R_type, not_5_out, not_6_out, not_7_out);
  and and_3 (sh, R_type, Instruction[12], not_8_out, not_9_out);
  and and_4 (sw, R_type, not_10_out, Instruction[13], not_11_out);
  Priority_Encoder #(.select_enc(2)) priority_encoder_1 (
    .in0(sb), .in1(sh), .in2(sw), .out(which_type));  // open: in3, gs, en_out, en_in
  Multiplexer #(.select(2), .width(32)) multiplexer_1 (
    .in0({{16{1'b0}}, DataFromReg[15:0]}), .in2({DataFromReg[15:0], {16{1'b0}}}), .out(sh_data),
    .sel(MemAddress[1:0]));  // open: in1, in3
  Multiplexer #(.select(2), .width(32)) multiplexer_2 (
    .in0({{24{1'b0}}, DataFromReg[7:0]}), .in1({{16{1'b0}}, DataFromReg[7:0], {8{1'b0}}}),
    .in2({{8{1'b0}}, DataFromReg[7:0], {16{1'b0}}}), .in3({DataFromReg[7:0], {24{1'b0}}}), .out(sb_data),
    .sel(MemAddress[1:0]));
  Multiplexer #(.select(2), .width(32)) multiplexer_3 (
    .in0(sb_data), .in1(sh_data), .in2(DataFromReg), .out(DataToMem), .sel(which_type));  // open: in3
  Multiplexer #(.select(2), .width(4)) multiplexer_4 (
    .in0(4'b0001), .in1(4'b0010), .in2(4'b0100), .in3(4'b1000), .out(sb_mask), .sel(MemAddress[1:0]));
  Multiplexer #(.select(2), .width(4)) multiplexer_5 (
    .in0(4'b0011), .in2(4'b1100), .out(sh_mask), .sel(MemAddress[1:0]));  // open: in1, in3
  Multiplexer #(.select(2), .width(4)) multiplexer_6 (
    .in0(sb_mask), .in1(sh_mask), .in2(4'b1111), .out(multiplexer_6_out), .sel(which_type));  // open: in3
  Multiplexer #(.width(4)) multiplexer_7 (.in0(4'b0000), .in1(multiplexer_6_out), .out(MemWriteMask), .sel(MemWEn));

  // Other names for the same wires on the sheet: D15_0[15:0] = DataFromReg[15:0]; D7_0[7:0] = DataFromReg[7:0];
  //   i2 = Instruction[2]; i3 = Instruction[3]; i4 = Instruction[4]; i5 = Instruction[5]; i6 = Instruction[6];
  //   i12 = Instruction[12]; i13 = Instruction[13]; i14 = Instruction[14]; A1_0[1:0] = MemAddress[1:0]

  // Notes on the sheet:
  //   INPUTS to your circuit
  //   DON'T CHANGE THE LOCATIONS OF THE INPUTS AND OUTPUTS!
  //   OUTPUT from your circuit
endmodule
